# Fritzing sketch Autonomous Vehicle (saved by Fritzing 0.9.3b)

parts:
  Raspberry_Pi_1 = Raspberry Pi 3 [part_number=RPI-3-V1.2]
  MD03A1 = Dual VNH2SP30 Motor Driver [part_number=MD03A]
  Part1 = PWM Shield
  MD03A2 = Dual VNH2SP30 Motor Driver [part_number=MD03A]
  Part2 = Arduino Uno (Rev3) - ICSP
  Part3 = SparkFun ESP8266 Thing
  U1 = TRANSCHIPTC5747 [package=camera_sfv24r-2st_2]  # not connected
  M1 = DC Motor
  M2 = DC Motor
  M3 = DC Motor
  M4 = DC Motor

nets:
  N1: Raspberry_Pi_1.GPIO2, Part1.GSCLK_-_D3
  N2: Raspberry_Pi_1.GPIO3, Part1.SIN_-_D11
  GND: Raspberry_Pi_1.GND, Part1.GND, Part1.GND_-_GND@1, MD03A2.GND, Part2.GND, Part3.GND
  N3: Raspberry_Pi_1.5V, Part1.5V_A
  N4: MD03A1.1INa, Part2.D13/SCK
  N5: MD03A1.1INb, Part2.D12/MISO
  N6: MD03A1.PWM, Part2.D11_PWM/MOSI
  N7: MD03A1.2PWM, Part2.D10_PWM/SS
  N8: MD03A1.2INb#142, Part2.D9_PWM
  N9: MD03A1.2INb#143, Part2.D8
  N10: MD03A1.OUT_1A, M1.pin_1
  N11: MD03A1.OUT_1B, M1.pin_2
  N12: MD03A1.OUT_2A, M2.pin_1
  N13: MD03A1.OUT_2B, M2.pin_2
  VCC: Part1.VCC, Part3.VCC
  N14: Part1.OUT0, Part2.A0
  N15: Part1.OUT1, Part2.A1
  N16: MD03A2.1INa, Part2.D7
  N17: MD03A2.1INb, Part2.D6_PWM
  N18: MD03A2.PWM, Part2.D5_PWM
  VIN: MD03A2.VIN, Part2.VIN
  N19: MD03A2.2PWM, Part2.D4
  N20: MD03A2.2INb#142, Part2.D3_PWM
  N21: MD03A2.2INb#143, Part2.D2
  N22: MD03A2.OUT_1A, M4.pin_1
  N23: MD03A2.OUT_1B, M4.pin_2
  N24: MD03A2.OUT_2A, M3.pin_1
  N25: MD03A2.OUT_2B, M3.pin_2
  N26: Part2.D0/RX, Part3.GPIO4
  5V: Part2.5V, Part3.VIN
